# Fritzing sketch v_plotter_v1 (saved by Fritzing 0.9.4)
breadboards: 1

parts:
  C1 = Electrolytic Capacitor [capacitance=1µF package="100 mil [THT, electrolytic]"]
  C2 = Electrolytic Capacitor [capacitance=1µF package="100 mil [THT, electrolytic]"]
  M1 = Stepper Motor - Bipolar
  M2 = Stepper Motor - Bipolar
  Power_plug1 = Power plug
  J1 = Basic Servo
  DRV_1 = DRV 8825 Stepper Motor Carrier, High Current [part_number="DRV 8825"]
  DRV_2 = DRV 8825 Stepper Motor Carrier, High Current [part_number="DRV 8825"]
  WeMos_D1_Mini1 = WeMos D1 Mini

nets:
  N1: C1.-, C2.-, Power_plug1.GND, DRV_1.GROUND_ST/_MT, DRV_2.GROUND_ST/_MT
  N2: C1.+, C2.+, Power_plug1.VCC, DRV_1.VOLTAGE_ST/_MT, DRV_2.VOLTAGE_ST/_MT
  N3: M1.A, DRV_2.OUT_1A
  N4: M1.C, DRV_2.OUT_2A
  N5: M1.B, DRV_2.OUT_1B
  N6: M1.D, DRV_2.OUT_2B
  N7: M2.A, DRV_1.OUT_1A
  N8: M2.C, DRV_1.OUT_2A
  N9: M2.B, DRV_1.OUT_1B
  N10: M2.D, DRV_1.OUT_2B
  N11: J1.gnd, DRV_1.GROUND_LOG, DRV_2.GROUND_LOG, WeMos_D1_Mini1.G
  VCC: J1.vcc, DRV_1.RESET, DRV_1.SLEEP, DRV_2.RESET, DRV_2.SLEEP, WeMos_D1_Mini1.5V
  N12: J1.pulse, WeMos_D1_Mini1.D0
  N13: DRV_1.STEP, WeMos_D1_Mini1.D6
  N14: DRV_1.DIRECTION, WeMos_D1_Mini1.D5
  N15: DRV_2.STEP, WeMos_D1_Mini1.D2
  N16: DRV_2.DIRECTION, WeMos_D1_Mini1.D1

notes:
  12V DC Power Supply
  Actual Servo Pins can vary. For me:
  VCC, Pulse, GND
  Be careful with connections between motor and driver board. This can change depending on the specific board and motor in use.
  100 uF

custom parts:
  DRV 8825 Stepper Motor Carrier, High Current: This is a Stepper Motor Controller for integrated circuits. This breakout board for TI’s DRV8825 microstepping bipolar stepper motor driver features adjustable current limiting, over-current and over-temperature protection, and six microstep resolutions (down to 1/32-step). It operates from 8.2 V to 45 V and can deliver up to approximately 1.5 A per phase without a heat sink or forced air flow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
