# Fritzing sketch v_plotter_additional (saved by Fritzing 0.9.4)
circuit board: 8.46667cm x 5.64444cm
breadboards: 1

parts:
  Capacitor2 = Electrolytic Capacitor [capacitance=1µF package="100 mil [THT, electrolytic]"]
  Capacitor1 = Electrolytic Capacitor [capacitance=1µF package="100 mil [THT, electrolytic]"]
  Motor_1 = Stepper Motor - Bipolar
  Motor2 = Stepper Motor - Bipolar
  Servo_D3 = Basic Servo
  DRV_2 = DRV 8825 Stepper Motor Carrier, High Current [part_number="DRV 8825"]
  DRV_1 = DRV 8825 Stepper Motor Carrier, High Current [part_number="DRV 8825"]
  WeMos_D1_Mini1 = WeMos D1 Mini
  Switch2 = SPST Switch [package=switch-spdt_kit]
  VCC1 = Battery
  Servo4 = Basic Servo
  Servo1 = Basic Servo
  Servo2 = Basic Servo
  Switch1 = SPST Switch [package=switch-spdt]
  Switch1_2 = SPST Switch [package=switch-spdt_kit]

nets:
  N1: Capacitor2.-, Capacitor1.-, DRV_2.GROUND_ST/_MT, DRV_1.GROUND_ST/_MT, VCC1.-
  N2: Capacitor2.+, Capacitor1.+, DRV_2.VOLTAGE_ST/_MT, DRV_1.VOLTAGE_ST/_MT, VCC1.+
  N3: Motor_1.A, DRV_1.OUT_1A
  N4: Motor_1.C, DRV_1.OUT_2A
  N5: Motor_1.B, DRV_1.OUT_1B
  N6: Motor_1.D, DRV_1.OUT_2B
  N7: Motor2.A, DRV_2.OUT_1A
  N8: Motor2.C, DRV_2.OUT_2A
  N9: Motor2.B, DRV_2.OUT_1B
  N10: Motor2.D, DRV_2.OUT_2B
  GND: Servo_D3.gnd, DRV_2.GROUND_LOG, DRV_1.GROUND_LOG, WeMos_D1_Mini1.G, Servo4.gnd, Servo1.gnd, Servo2.gnd
  VCC: Servo_D3.vcc, DRV_2.RESET, DRV_2.SLEEP, DRV_1.RESET, DRV_1.SLEEP, WeMos_D1_Mini1.5V, Switch2.P, Servo4.vcc, Servo1.vcc, Servo2.vcc, Switch1.P, Switch1_2.P
  N11: Servo_D3.pulse, WeMos_D1_Mini1.D4
  N12: DRV_2.MS2, Switch2.S
  N13: DRV_2.MS3, Switch2.O
  N14: DRV_2.STEP, WeMos_D1_Mini1.D6
  N15: DRV_2.DIRECTION, WeMos_D1_Mini1.D5
  N16: DRV_1.MS2, Switch1.S, Switch1_2.S
  N17: DRV_1.MS3, Switch1.O, Switch1_2.O
  N18: DRV_1.STEP, WeMos_D1_Mini1.D2
  N19: DRV_1.DIRECTION, WeMos_D1_Mini1.D1
  N20: WeMos_D1_Mini1.D0, Servo1.pulse
  N21: WeMos_D1_Mini1.D3, Servo4.pulse
  N22: WeMos_D1_Mini1.D7, Servo2.pulse

notes:
  12V DC Power Supply
  Actual Servo Pins can vary. For me:
  VCC, Pulse, GND
  Be careful with connections between motor and driver board. This can change depending on the specific board and motor in use.
  100 uF

custom parts:
  DRV 8825 Stepper Motor Carrier, High Current: This is a Stepper Motor Controller for integrated circuits. This breakout board for TI’s DRV8825 microstepping bipolar stepper motor driver features adjustable current limiting, over-current and over-temperature protection, and six microstep resolutions (down to 1/32-step). It operates from 8.2 V to 45 V and can deliver up to approximately 1.5 A per phase without a heat sink or forced air flow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
